# Fritzing sketch Verkabelung (saved by Fritzing 0.9.4)
breadboards: 1

parts:
  MCU1 = Raspberry Pi Zero
  S1 = Pushbutton [package="[THT]"]
  S2 = Square Pushbutton
  Bauteil1 = 12 NeoPixel Ring [part_number=1643]
  S3 = Pushbutton [package="[THT]"]

nets:
  N1: MCU1.pin_2, MCU1.pin_4, MCU1.pin_6, MCU1.pin_20, S2.leg1
  N2: MCU1.pin_12, Bauteil1.IN
  N3: MCU1.pin_16, S1.Pin_3, S1.Pin_4
  N4: MCU1.pin_38, S3.Pin_3, S3.Pin_4
  N5: S1.Pin_1, S1.Pin_2, Bauteil1.GND, S3.Pin_1, S3.Pin_2
  N6: S2.leg0, Bauteil1.VDD

custom parts:
  12 NeoPixel Ring: 12 ultra bright smart LED NeoPixels are arranged in a circle with 1.5" (37mm) outer diameter. The rings are 'chainable' - connect the output pin of one to the input pin of another. Use only one microcontroller pin to control as many as you can chain together! Each LED is addressable as the driver chip is inside the LED. Each one has ~18mA constant current drive so the color will be very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
